# Fritzing sketch NodeMcu_WebServ_height (saved by Fritzing 0.9.3b)

parts:
  U1 = 2-Channel 5v Relay Shield [package=relay-2ch5v10a]
  HC-SR04_Sensor_1 = HC-SR04 Ultrasonic Distance Sensor
  U2 = NodeMCU V1.0

nets:
  VCC: U1.VCC, HC-SR04_Sensor_1.VCC, U2.Vin
  GND: U1.GND, HC-SR04_Sensor_1.GND, U2.GND
  N1: U1.IN1, U2.D2
  N2: U1.IN2, U2.D3
  N3: HC-SR04_Sensor_1.TRIG, U2.D0
  N4: HC-SR04_Sensor_1.ECHO, U2.D1

custom parts:
  2-Channel 5v Relay Shield: 2 Channel 5v Relay Shield w. 2x SPD-06VDC-SD-C
  NodeMCU V1.0: ESP8266 based NodeMCU
